// Logisim project lab07.circ as structural Verilog
module main (
  input  PB0
);

  wire clock_1_out, clock_controller_1_p4, counter_256_1_p1, counter_256_1_p3, ledbar_1_p1, piso_1_p5,
       rom_256_8_1_p5, rom_256_8_1_p6, sequence_detector_1_p6;
  wire [3:0] sequence_detector_1_p5;
  wire [7:0] counter_256_1_p2, rom_256_8_1_p4;

  Clock clock_1 (.out(clock_1_out));
  // counter_256 counter_256_1: pin names not known; wires that end beside it: counter_256_1_p1, counter_256_1_p2, counter_256_1_p3
  and and_1 (clock_1_out, PB0, sequence_detector_1_p6);
  Hex_Digit_Display hex_digit_display_1 (.value(counter_256_1_p2[7:4]));  // open: dp
  Hex_Digit_Display hex_digit_display_2 (.value(counter_256_1_p2[3:0]));  // open: dp
  // ROM_256_8 rom_256_8_1: pin names not known; wires that end beside it: counter_256_1_p1, counter_256_1_p2, counter_256_1_p3, rom_256_8_1_p4, rom_256_8_1_p5, rom_256_8_1_p6
  // clock_controller clock_controller_1: pin names not known; wires that end beside it: PB0, clock_1_out, counter_256_1_p1, clock_controller_1_p4, counter_256_1_p3, rom_256_8_1_p5, rom_256_8_1_p6
  Hex_Digit_Display hex_digit_display_3 (.value(rom_256_8_1_p4[7:4]));  // open: dp
  Hex_Digit_Display hex_digit_display_4 (.value(rom_256_8_1_p4[3:0]));  // open: dp
  // LedBar #(.inputtype("row")) ledbar_1: pin names not known; wires that end beside it: ledbar_1_p1
  // piso piso_1: pin names not known; wires that end beside it: rom_256_8_1_p4, rom_256_8_1_p5, rom_256_8_1_p6, ledbar_1_p1, piso_1_p5, piso_1_p5, rom_256_8_1_p6, clock_controller_1_p4
  Hex_Digit_Display hex_digit_display_5 (.value(sequence_detector_1_p5));  // open: dp
  // sequence_detector sequence_detector_1: pin names not known; wires that end beside it: piso_1_p5, piso_1_p5, rom_256_8_1_p6, clock_controller_1_p4, sequence_detector_1_p5, sequence_detector_1_p6

  // Notes on the sheet:
  //   CLK_DIV
endmodule

// VHDL entity piso, as the project stores it:
library ieee;
use ieee.std_logic_1164.all;

entity piso is
port(
	parallel_in: in std_logic_vector(7 downto 0);
	parallel_out: out std_logic_vector(7 downto 0);
	load_not, clock: in std_logic;
	serial_out: out std_logic
);
end;

architecture behav of piso is
	signal combined_clock: std_logic;
	signal data: std_logic_vector(7 downto 0);
begin
	combined_clock <= load_not and clock;
	parallel_out <= data;

	process (combined_clock) is
		variable next_data: std_logic_vector(7 downto 0);
	begin
		serial_out <= data(7);
		if (falling_edge(combined_clock)) then
			if (load_not = '0') then
				data <= parallel_in;
			else
				data <= data(6 downto 0) & '0';
			end if;
		end if;
	end process;
end;

// VHDL entity sequence_detector, as the project stores it:
library ieee;
use ieee.std_logic_1164.all;

entity sequence_detector is
port(
	serial_in, clock, reset_not: in std_logic;
	state_out: out std_logic_vector(3 downto 0);
	is_detected: out std_logic
);
end;

architecture state_machine of sequence_detector is
	type state is (s0, s1, s2, s3, s4, s5, s6, s7);
	signal st: state := s0;
	signal combined_clock: std_logic := '1';
begin
	state_out <= "0000" when st = s0 else
					 "0001" when st = s1 else
					 "0010" when st = s2 else
					 "0011" when st = s3 else
					 "0100" when st = s4 else
					 "0101" when st = s5 else
					 "0110" when st = s6 else
					 "0111" when st = s7 else
					 "0000";

	is_detected <= '1' when st = s7 else '0';
	combined_clock <= clock and reset_not;
	process (combined_clock)
	begin
		if (falling_edge(combined_clock)) then
			if (reset_not = '0') then
				st <= s0;
			elsif (serial_in = '1') then
				case st is
					when s0 => st <= s1;
					when s1 => st <= s2;
					when s2 => st <= s3;
					when s3 => st <= s3;
					when s4 => st <= s5;
					when s5 => st <= s2;
					when s6 => st <= s1;
					when s7 => st <= s1;
					when others => st <= s0;
				end case;
			else
				case st is
					when s0 => st <= s0;
					when s1 => st <= s0;
					when s2 => st <= s0;
					when s3 => st <= s4;
					when s4 => st <= s0;
					when s5 => st <= s6;
					when s6 => st <= s7;
					when s7 => st <= s0;
					when others => st <= s0;
				end case;
			end if;
		end if;
	end process;
end;

// VHDL entity ROM_256_8, as the project stores it:
-- megafunction wizard: %ROM: 1-PORT%
-- GENERATION: STANDARD
-- VERSION: WM1.0
-- MODULE: altsyncram 

-- ============================================================
-- File Name: ROM_256_8.vhd
-- Megafunction Name(s):
-- 			altsyncram
--
-- Simulation Library Files(s):
-- 			altera_mf
-- ============================================================
-- ************************************************************
-- THIS IS A WIZARD-GENERATED FILE. DO NOT EDIT THIS FILE!
--
-- 18.1.0 Build 625 09/12/2018 SJ Lite Edition
-- ************************************************************


--Copyright (C) 2018  Intel Corporation. All rights reserved.
--Your use of Intel Corporation's design tools, logic functions 
--and other software and tools, and its AMPP partner logic 
--functions, and any output files from any of the foregoing 
--(including device programming or simulation files), and any 
--associated documentation or information are expressly subject 
--to the terms and conditions of the Intel Program License 
--Subscription Agreement, the Intel Quartus Prime License Agreement,
--the Intel FPGA IP License Agreement, or other applicable license
--agreement, including, without limitation, that your use is for
--the sole purpose of programming logic devices manufactured by
--Intel and sold by Intel or its authorized distributors.  Please
--refer to the applicable agreement for further details.


LIBRARY ieee;
USE ieee.std_logic_1164.all;

LIBRARY altera_mf;
USE altera_mf.altera_mf_components.all;

ENTITY ROM_256_8 IS
	PORT
	(
		address		: IN STD_LOGIC_VECTOR (7 DOWNTO 0);
		clock		: IN STD_LOGIC;
		q		: OUT STD_LOGIC_VECTOR (7 DOWNTO 0)
	);
END ROM_256_8;


ARCHITECTURE SYN OF rom_256_8 IS

	SIGNAL sub_wire0	: STD_LOGIC_VECTOR (7 DOWNTO 0);

BEGIN
	q    <= sub_wire0(7 DOWNTO 0);

	altsyncram_component : altsyncram
	GENERIC MAP (
		address_aclr_a => "NONE",
		clock_enable_input_a => "BYPASS",
		clock_enable_output_a => "BYPASS",
		init_file => "ROM_256_8.hex",
		intended_device_family => "MAX 10",
		lpm_hint => "ENABLE_RUNTIME_MOD=NO",
		lpm_type => "altsyncram",
		numwords_a => 256,
		operation_mode => "ROM",
		outdata_aclr_a => "NONE",
		outdata_reg_a => "UNREGISTERED",
		widthad_a => 8,
		width_a => 8,
		width_byteena_a => 1
	)
	PORT MAP (
		address_a => address,
		clock0 => clock,
		q_a => sub_wire0
	);



END SYN;

-- ============================================================
-- CNX file retrieval info
-- ============================================================
-- Retrieval info: PRIVATE: ADDRESSSTALL_A NUMERIC "0"
-- Retrieval info: PRIVATE: AclrAddr NUMERIC "0"
-- Retrieval info: PRIVATE: AclrByte NUMERIC "0"
-- Retrieval info: PRIVATE: AclrOutput NUMERIC "0"
-- Retrieval info: PRIVATE: BYTE_ENABLE NUMERIC "0"
-- Retrieval info: PRIVATE: BYTE_SIZE NUMERIC "8"
-- Retrieval info: PRIVATE: BlankMemory NUMERIC "0"
-- Retrieval info: PRIVATE: CLOCK_ENABLE_INPUT_A NUMERIC "0"
-- Retrieval info: PRIVATE: CLOCK_ENABLE_OUTPUT_A NUMERIC "0"
-- Retrieval info: PRIVATE: Clken NUMERIC "0"
-- Retrieval info: PRIVATE: IMPLEMENT_IN_LES NUMERIC "0"
-- Retrieval info: PRIVATE: INIT_FILE_LAYOUT STRING "PORT_A"
-- Retrieval info: PRIVATE: INIT_TO_SIM_X NUMERIC "0"
-- Retrieval info: PRIVATE: INTENDED_DEVICE_FAMILY STRING "MAX 10"
-- Retrieval info: PRIVATE: JTAG_ENABLED NUMERIC "0"
-- Retrieval info: PRIVATE: JTAG_ID STRING "NONE"
-- Retrieval info: PRIVATE: MAXIMUM_DEPTH NUMERIC "0"
-- Retrieval info: PRIVATE: MIFfilename STRING "ROM_256_8.hex"
-- Retrieval info: PRIVATE: NUMWORDS_A NUMERIC "256"
-- Retrieval info: PRIVATE: RAM_BLOCK_TYPE NUMERIC "0"
-- Retrieval info: PRIVATE: RegAddr NUMERIC "1"
-- Retrieval info: PRIVATE: RegOutput NUMERIC "0"
-- Retrieval info: PRIVATE: SYNTH_WRAPPER_GEN_POSTFIX STRING "0"
-- Retrieval info: PRIVATE: SingleClock NUMERIC "1"
-- Retrieval info: PRIVATE: UseDQRAM NUMERIC "0"
-- Retrieval info: PRIVATE: WidthAddr NUMERIC "8"
-- Retrieval info: PRIVATE: WidthData NUMERIC "8"
-- Retrieval info: PRIVATE: rden NUMERIC "0"
-- Retrieval info: LIBRARY: altera_mf altera_mf.altera_mf_components.all
-- Retrieval info: CONSTANT: ADDRESS_ACLR_A STRING "NONE"
-- Retrieval info: CONSTANT: CLOCK_ENABLE_INPUT_A STRING "BYPASS"
-- Retrieval info: CONSTANT: CLOCK_ENABLE_OUTPUT_A STRING "BYPASS"
-- Retrieval info: CONSTANT: INIT_FILE STRING "ROM_256_8.hex"
-- Retrieval info: CONSTANT: INTENDED_DEVICE_FAMILY STRING "MAX 10"
-- Retrieval info: CONSTANT: LPM_HINT STRING "ENABLE_RUNTIME_MOD=NO"
-- Retrieval info: CONSTANT: LPM_TYPE STRING "altsyncram"
-- Retrieval info: CONSTANT: NUMWORDS_A NUMERIC "256"
-- Retrieval info: CONSTANT: OPERATION_MODE STRING "ROM"
-- Retrieval info: CONSTANT: OUTDATA_ACLR_A STRING "NONE"
-- Retrieval info: CONSTANT: OUTDATA_REG_A STRING "UNREGISTERED"
-- Retrieval info: CONSTANT: WIDTHAD_A NUMERIC "8"
-- Retrieval info: CONSTANT: WIDTH_A NUMERIC "8"
-- Retrieval info: CONSTANT: WIDTH_BYTEENA_A NUMERIC "1"
-- Retrieval info: USED_PORT: address 0 0 8 0 INPUT NODEFVAL "address[7..0]"
-- Retrieval info: USED_PORT: clock 0 0 0 0 INPUT VCC "clock"
-- Retrieval info: USED_PORT: q 0 0 8 0 OUTPUT NODEFVAL "q[7..0]"
-- Retrieval info: CONNECT: @address_a 0 0 8 0 address 0 0 8 0
-- Retrieval info: CONNECT: @clock0 0 0 0 0 clock 0 0 0 0
-- Retrieval info: CONNECT: q 0 0 8 0 @q_a 0 0 8 0
-- Retrieval info: GEN_FILE: TYPE_NORMAL ROM_256_8.vhd TRUE
-- Retrieval info: GEN_FILE: TYPE_NORMAL ROM_256_8.inc FALSE
-- Retrieval info: GEN_FILE: TYPE_NORMAL ROM_256_8.cmp TRUE
-- Retrieval info: GEN_FILE: TYPE_NORMAL ROM_256_8.bsf TRUE
-- Retrieval info: GEN_FILE: TYPE_NORMAL ROM_256_8_inst.vhd TRUE
-- Retrieval info: LIB_FILE: altera_mf

// VHDL entity counter_256, as the project stores it:
LIBRARY ieee;
USE ieee.std_logic_1164.all;
use ieee.numeric_std.all;

ENTITY counter_256 IS
  PORT (
  	clk: in std_logic;
  	q: out std_logic_vector(7 downto 0)
  );
END counter_256;


ARCHITECTURE TypeArchitecture OF counter_256 IS
BEGIN
	counter_mod256: process(clk) is
		variable counter: natural := 0;
	begin 
		if (falling_edge(clk)) then
			if (counter = 255) then 
				counter := 0;
			else 
				counter := counter + 1;
			end if;
			q <= std_logic_vector(to_unsigned(counter, 8));
		end if;
	end process counter_mod256;
END TypeArchitecture;

// VHDL entity clock_controller, as the project stores it:
LIBRARY ieee;
USE ieee.std_logic_1164.all;

ENTITY clock_controller IS
  PORT (
  	clk_geral, enable: in std_logic;
  	clk_counter, reset_sequence, clk_memo, piso_load, clk_serial: out std_logic
  );
END clock_controller;

ARCHITECTURE TypeArchitecture OF clock_controller IS
BEGIN
	process(clk_geral) is
		constant N: integer := 25;
		variable counter: integer := 0;
	begin
		if (falling_edge(clk_geral)) then
			if enable = '0' then
				if counter = N then
					counter := 0;
				else
					counter := counter + 1;
				end if;
			end if;

			if counter = 0 then
				clk_counter <= '1';
				reset_sequence <= '0';
			else
				clk_counter <= '0';
				reset_sequence <= '1';
			end if;

			if counter = 1 then
				clk_memo <= '0';
			else
				clk_memo <= '1';
			end if;
	
			if counter = 5 then
				piso_load <= '0';
			else
				piso_load <= '1';
			end if;

			case counter is
				when 7|9|11|13|15|17|19|21 => clk_serial <= '0';
				when others => clk_serial <= '1';
			end case;
		end if;
	end process;
END TypeArchitecture;
